# Fritzing sketch pic-serprog_noyito (saved by Fritzing 1.0.6)
breadboards: 1

parts:
  R1 = Resistor [tolerance=±5% power=0.25W resistance=4.7k package=THT]
  JP1 = Header 6 [package=molex-1x6-ra]
  Pico_H1 = rpi_picoh

nets:
  N1: R1.Pin_0, Pico_H1.connector38
  N2: R1.Pin_1, JP1.3
  N3: JP1.1, Pico_H1.connector5
  N4: JP1.2, Pico_H1.connector42
  N5: JP1.4, Pico_H1.connector3
  N6: JP1.5, Pico_H1.connector40
  N7: JP1.6, Pico_H1.connector39
