# Fritzing sketch pico-serprog_dip-8 (saved by Fritzing 1.0.6)
breadboards: 1

parts:
  R1 = Resistor [tolerance=±5% power=0.25W resistance=4.7k package=THT]
  Pico_H1 = rpi_picoh

nets:
  N1: R1.Pin_1, Pico_H1.connector38
